# Fritzing sketch DelayedButton (saved by Fritzing 0.9.1b)
breadboards: 1

parts:
  Part1 = Arduino Micro (Rev3)  # not connected
  S1 = Pushbutton [package="[THT]"]
  R1 = Resistor [tolerance=±5% resistance=10k package=THT]
  LED1 = LED - 5mm [color="Red (633nm)" package="5 mm [THT]"]
  R2 = Resistor [tolerance=±5% resistance=220 package=THT]
  R3 = Resistor [tolerance=±5% resistance=10k package=THT]
  S2 = Pushbutton [package="[THT]"]

nets:
  N1: S1.Pin_1, S1.Pin_2, LED1.anode, S2.Pin_1, S2.Pin_2
  N2: S1.Pin_3, S1.Pin_4, R1.Pin_1
  N3: R1.Pin_0, R3.Pin_0
  N4: LED1.cathode, R2.Pin_0
  N5: R3.Pin_1, S2.Pin_3, S2.Pin_4
